// Logisim project comboROM.circ as structural Verilog
module Cominational_ROM (
  input  in_1,
  input  in_2,
  input  in_3,
  input  in_4,
  input  in_5,
  input  in_6,
  input  in_7,
  input  in_8,
  output Out2,
  output Out1,
  output Out0
);

  ROM #(.dataWidth(3)) rom_1 (
    .addr({in_1, in_2, in_3, in_4, in_5, in_6, in_7, in_8}), .data({Out2, Out1, Out0}));  // open: sel

  // Notes on the sheet:
  //   contents of rom_1 (hex, n*v repeats v):
  //   4 1 6 0 3 5 7 2 0 0 1 8*0 6 0 1 26*0 16*4 48*0 16*2 16*7 16*3 32*0 16*5 32*0 16*1
endmodule
